# Fritzing sketch Chamber-Wiring (saved by Fritzing 1.0.4)
breadboards: 1

parts:
  Part3 = Adafruit Pi Cobbler Plus [part_number="Adafruit #2029"]
  Part5 = OLED Monochrome 128x32 SPI [part_number=661]
  S1 = Pushbutton [package="[THT]"]
  S2 = Pushbutton [package="[THT]"]
  4-pin_PWM_fan1 = Header 4 [package=screwterminal-3.5mm-4_lock]
  4-pin_PWM_fan2 = Header 4 [package=screwterminal-3.5mm-4_lock]
  DS1 = DS18B20 1-Wire Temperature Sensor [part_number=DS18B20]
  R1 = Resistor [tolerance=±5% resistance=4.7 package="0603 [SMD]"]  # not connected
  M1 = MDD10A

nets:
  +5V: Part3.SDA, Part3.+5V, Part3.+3.3V, Part3.GPIO24, 4-pin_PWM_fan1.2, 4-pin_PWM_fan2.2, DS1.VDD
  N1: Part3.GPIO17, Part3.GPIO18, 4-pin_PWM_fan1.4
  N2: Part3.GPIO22, Part3.GPIO23, 4-pin_PWM_fan2.4, M1.PWM1
  GND: Part3.MOSI, Part3.GPIO5, Part3.CE1, Part3.GND, Part3.SCL, Part3.RXD, Part3.GPIO27, Part3.GPIO13, Part3.GPIO21, 4-pin_PWM_fan1.1, 4-pin_PWM_fan2.1, M1.Bat-, M1.GND
  N3: Part3.SCLK, Part3.CE0
  N4: Part3.EEDAT, Part3.EECLK
  N5: Part3.GPIO19, Part3.GPIO16
  N6: Part3.GPIO26, Part3.GPIO20
  N7: Part3.TXD, Part3.GPIO4
  N8: Part3.GPIO25, Part3.MISO
  N9: Part3.GPIO12, Part3.GPIO6
  GND_2: Part5.GND, DS1.GND
  N10: S1.Pin_1, S1.Pin_2
  N11: S1.Pin_3, S1.Pin_4
  N12: S2.Pin_1, S2.Pin_2
  N13: S2.Pin_3, S2.Pin_4

custom parts:
  Adafruit Pi Cobbler Plus: The Raspberry Pi B+/Pi 2/ Pi 3 has landed on the Maker World like a 40-GPIO pinned, quad-USB ported, credit card sized bomb of DIY joy. And while you can use most of our great Model B accessories by hooking up our downgrade cable, its probably a good time to upgrade your set up and accessorize using all of the Model B+'s / Pi 2's / Pi 3's 40 pins. That's why we now carry the Adafruit Assembled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
  OLED Monochrome 128x32 SPI: These displays are small, only about 1" diagonal, but very readable due to the high contrast of an OLED display. This display is made of 128x32 individual white OLED pixels, each one is turned on or off by the controller chip. Because the display makes its own light, no backlight is required. This reduces the power required to run the OLED and is why the display has such high contrast; we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
